# Fritzing sketch L293MotorBoard (saved by Fritzing 0.9.3b)
circuit board: 8.46667cm x 5.64444cm
breadboards: 1

parts:
  L293 = L293D [package=THT]
  < = Resistor [tolerance=±5% resistance=220 package=THT]
  <_2 = Resistor [tolerance=±5% resistance=220 package=THT]
  <_3 = Resistor [tolerance=±5% resistance=220 package=THT]
  <_4 = Resistor [tolerance=±5% resistance=220 package=THT]
  <_5 = Resistor [tolerance=±5% resistance=220 package=THT]
  <_6 = Resistor [tolerance=±5% resistance=220 package=THT]
  <_7 = Resistor [tolerance=±5% resistance=220 package=THT]
  <_8 = Resistor [tolerance=±5% resistance=220 package=THT]
  Motor1 = female pin header, 7 pins [form="♀ (female)"]
  Motor2 = female pin header, 7 pins [form="♀ (female)"]
  R1 = Resistor [tolerance=±5% resistance=10k package=THT]
  R2 = Resistor [tolerance=±5% resistance=10k package=THT]

nets:
  N1: L293.Enable_1, Motor1.pin7, R1.Pin_0
  N2: L293.In_1, Motor1.pin6
  N3: L293.Out_1_(_Controlled_by_Enable_1_), <_2.Pin_1, <_3.Pin_0, Motor1.pin4
  N4: L293.0V, <.Pin_1, <_3.Pin_1, <_4.Pin_1, <_8.Pin_1, Motor1.pin1, Motor2.pin1, R1.Pin_1, R2.Pin_0
  N5: L293.Out_2_(_Controlled_by_Enable_1_), <_4.Pin_0, <_5.Pin_1, Motor1.pin3
  N6: L293.In_2, Motor1.pin5
  N7: L293.+Vmotor, <_2.Pin_0, <_5.Pin_0, <_6.Pin_0, <_7.Pin_0, Motor1.pin2
  N8: L293.Enable_2, Motor2.pin7, R2.Pin_1
  N9: L293.In_3, Motor2.pin6
  N10: L293.Out_3_(_Controlled_by_Enable_2_), <_7.Pin_1, <_8.Pin_0, Motor2.pin4
  N11: L293.Out_4_(_Controlled_by_Enable_2_), <.Pin_0, <_6.Pin_1, Motor2.pin3
  N12: L293.In_4, Motor2.pin5
  N13: L293.+V, Motor2.pin2

notes:
  Vc
  GND
  Vm
  M2O1
  M2O2
  M2D1
  M2D2
  M2PWM
  M1PWM
  M1D2
  M1D1
  M1O2
  M1O1
