# Fritzing sketch MotorController (saved by Fritzing 0.9.3b)
circuit board: 6.34044cm x 4.3461cm
breadboards: 1

parts:
  27524 = IC, DIP package, 8 pins [chip_label="Gate Driver"]
  HK19F-DC5V = DS2Y-5-DC5V [part_number=HK19F-DC5V]
  HK19F-DC5V_2 = DS2Y-5-DC5V [part_number=HK19F-DC5V]
  R1 = Resistor [tolerance=±5% resistance=10k package=THT]
  R3 = Resistor [tolerance=±5% resistance=10k package=THT]
  J1 = female pin header, 12 pins [form="♀ (female)"]
  D3 = Rectifier Diode [part_number=1N4001 package="300 mil [THT]"]
  D4 = Rectifier Diode [part_number=1N4001 package="300 mil [THT]"]
  R2 = Resistor [tolerance=±5% resistance=6.8k package=THT]
  R4 = Resistor [tolerance=±5% resistance=6.8k package=THT]
  C3 = Ceramic Capacitor [capacitance=1µF voltage=35V package="100 mil [THT, multilayer]"]
  C1 = Ceramic Capacitor [capacitance=1µF voltage=35V package="100 mil [THT, multilayer]"]
  R5 = Resistor [tolerance=±5% resistance=220 package=THT]
  R6 = Resistor [tolerance=±5% resistance=220 package=THT]
  C2 = Ceramic Capacitor [capacitance=1µF voltage=35V package="100 mil [THT, multilayer]"]
  C4 = Ceramic Capacitor [capacitance=1µF voltage=35V package="100 mil [THT, multilayer]"]

nets:
  N1: 27524.pin1, J1.pin2
  N2: 27524.pin2, R3.Pin_1, R4.Pin_1
  N3: 27524.pin3, HK19F-DC5V.8_N.O., HK19F-DC5V.1_+, HK19F-DC5V.13_COM, HK19F-DC5V_2.4_COM, HK19F-DC5V_2.16_-, HK19F-DC5V_2.9_N.O., J1.pin6, D3.anode, D4.anode, R2.Pin_0, R4.Pin_0, C3.0, C1.1, C2.1, C4.0
  N4: 27524.pin4, R1.Pin_1, R2.Pin_1
  N5: 27524.pin5, R5.Pin_1
  N6: 27524.pin6, J1.pin12
  N7: 27524.pin7, R6.Pin_1
  N8: 27524.pin8, J1.pin10
  N9: HK19F-DC5V.6_N.C., J1.pin4
  N10: HK19F-DC5V.4_COM, HK19F-DC5V.9_N.O., C3.1, R6.Pin_0, C4.1
  N11: HK19F-DC5V.16_-, J1.pin1, D4.cathode
  N12: HK19F-DC5V.11_N.C., J1.pin3
  N13: HK19F-DC5V_2.8_N.O., HK19F-DC5V_2.13_COM, C1.0, R5.Pin_0, C2.0
  N14: HK19F-DC5V_2.6_N.C., J1.pin9
  N15: HK19F-DC5V_2.1_+, J1.pin11, D3.cathode
  N16: HK19F-DC5V_2.11_N.C., J1.pin8
  N17: R1.Pin_0, J1.pin7
  N18: R3.Pin_0, J1.pin5

notes:
  GND
  INA
  INB
  VDD
  OUTA1
  OUTA2
  ENB
  OUTB1
  ENA
  OUTB2
  DIRA
  DIRB
  (5v PWM)
  (5v high/low)
  Motor Driver  v.1
  ©2018 That Ain't Working, All Rights Reserved  http://thataintworking.com
